# Fritzing sketch schematic (saved by Fritzing 0.9.1b)

parts:
  Pro_Micro1 = Pro Micro
  R1 = Resistor [tolerance=±5% resistance=1k package=THT]
  R2 = Resistor [tolerance=±5% resistance=1k package=THT]
  LED1 = LED - 5mm [color="Green (555nm)" package="5 mm [THT]"]
  LED2 = LED - 5mm [color="Yellow (592nm)" package="5 mm [THT]"]
  CONN1 = USB connector [package=THT]
  JP1 = Header 3 [package=molex-1x3_lock]
  R3 = Resistor [tolerance=±5% resistance=1M package=THT]
  R4 = Resistor [tolerance=±5% resistance=470 package=THT]

nets:
  GND: Pro_Micro1.GND, LED1.cathode, LED2.cathode, JP1.1, R3.Pin_1
  N1: Pro_Micro1.D2, JP1.2
  N2: Pro_Micro1.D3, R3.Pin_0, R4.Pin_1
  N3: Pro_Micro1.D4, R1.Pin_0
  N4: Pro_Micro1.D5, R2.Pin_0
  N5: R1.Pin_1, LED1.anode
  N6: R2.Pin_1, LED2.anode
  N7: CONN1.GND, CONN1.chassis5, CONN1.chassis6
  N8: JP1.3, R4.Pin_0

custom parts:
  Pro Micro: The SparkFun Pro Micro is a complete USB-based microcontoller development system, in a very small footprint, capable of implementing many types of projects. All programming can be done via the USB port.

// code stored in the sketch: tsa.ino
/*
 *** USAGE
 *
 * This program provides a serial interface adapter to the Medoc TSA-II.
 *
 * When connected to a serial port, it will communicate at 9600 baud.
 * To instruct the TSA to start, send a single '*' character (with no line break).
 * To receive output from the TSA, listen for a '#' character.
 *
 * The status LED will blink:
 *  - 4x when the device first starts
 *  - 3x when the TSA was instructed to start
 *  - 2x when output was received from the TSA
 *  - 1x if an unknown command or character is received
 *
 *
 *** NOTES
 *
 * See the Medoc TSA-II FAQ (http://www.medoc-web.com/support/faq)
 *
 *  TTL input option:
 *    The TSA can be started by an external ±5V, 100-2000msec trigger.
 *    The trigger must be set to External in the CoVAS program algorithm.
 *
 *  TTL output option:
 *    TTL output is a ±5V, duration 50-3000msec pulse (set via Utility-»Setup).
 *    TTL output must be enabled in the CoVAS program algorithm.
 *
 * The '±' part is probably an error.
 *
 *
 *** COPYRIGHT
 *
 * written for Carissa Cascio
 * Vanderbilt University Medical Center
 * 2015
 *
 */


// I/O pins
#define TSA_OUTPUT_PIN  13  // to TSA-II TTL Out
#define TSA_INPUT_PIN   12  // to TSA-II TTL In
#define STATUS_PIN      11  // LED indicator
#define ACTIVITY_PIN    10  // LED indicator

// `setup` runs once when you press reset or power on.
void setup() {
    // initialize
    pinMode(TSA_OUTPUT_PIN, OUTPUT);
    pinMode(TSA_INPUT_PIN, INPUT);
    pinMode(STATUS_PIN, OUTPUT);
    pinMode(ACTIVITY_PIN, OUTPUT);
    Serial.begin(9600);

    // indicate a successful initialization
    blinkStatus(4);
    delay(1000);
}

// `receivedPulse` returns true only for a 50-3000ms pulse
bool receivedPulse() {
    unsigned long start = millis();

    do {
        // check if the pulse has ended
        if (!digitalRead(TSA_OUTPUT_PIN)) {
            // make sure the pulse was longer than 50ms
            return millis() - start > 50;
        }
    } while (millis() - start < 3000);

    // the pulse lasted longer than 3000ms
    return false;
}

// `sendTriggerPulse` sends a 200ms pulse to the TSA
void sendTriggerPulse() {
    digitalWrite(TSA_INPUT_PIN, HIGH);
    delay(200);
    digitalWrite(TSA_INPUT_PIN, LOW);
}

// `blinkStatus` flashes an LED n times
void blinkStatus(int n) {
    for (int i = 0; i < n; i++) {
        digitalWrite(STATUS_PIN, HIGH);
        delay(200);
        digitalWrite(STATUS_PIN, LOW);
        delay(200);
    }
}

// `loop` runs repeatedly
void loop() {

    // check if the TSA appears to be sending a signal
    if (digitalRead(TSA_OUTPUT_PIN)) {
        // wait for the pulse to end
        digitalWrite(ACTIVITY_PIN, HIGH);
        bool pulsed = receivedPulse();
        digitalWrite(ACTIVITY_PIN, LOW);
        // if we got a valid pulse, send a signal back
        if (pulsed) {
            Serial.print("#");
            blinkStatus(2);
        }
    }

    // check if we received a start command
    if (Serial.available() > 0) {
        // read the incoming byte:
        char cmd = Serial.read();
        // trigger command
        if (cmd == '*') {
            sendTriggerPulse();
            blinkStatus(3);
        }
        // received an unknown command
        else {
            blinkStatus(1);
        }
    }
}
